// Logisim project BD.circ as structural Verilog: 3 circuits, main circuit main
module main (
  input  Clock,
  input  Clear,
  input  [7:0] Dado,
  output [7:0] \Saída 
);

  D_Flip_Flop d_ff_1 (.clk(Clock), .D(Dado[7]), .Q(\Saída [7]), .reset(Clear));  // open: Qn, preset, en
  D_Flip_Flop d_ff_2 (.clk(Clock), .D(Dado[6]), .Q(\Saída [6]), .reset(Clear));  // open: Qn, preset, en
  D_Flip_Flop d_ff_3 (.clk(Clock), .D(Dado[5]), .Q(\Saída [5]), .reset(Clear));  // open: Qn, preset, en
  D_Flip_Flop d_ff_4 (.clk(Clock), .D(Dado[4]), .Q(\Saída [4]), .reset(Clear));  // open: Qn, preset, en
  D_Flip_Flop d_ff_5 (.clk(Clock), .D(Dado[3]), .Q(\Saída [3]), .reset(Clear));  // open: Qn, preset, en
  D_Flip_Flop d_ff_6 (.clk(Clock), .D(Dado[2]), .Q(\Saída [2]), .reset(Clear));  // open: Qn, preset, en
  D_Flip_Flop d_ff_7 (.clk(Clock), .D(Dado[1]), .Q(\Saída [1]), .reset(Clear));  // open: Qn, preset, en
  D_Flip_Flop d_ff_8 (.clk(Clock), .D(Dado[0]), .Q(\Saída [0]), .reset(Clear));  // open: Qn, preset, en
endmodule

module BR (
  input  Clear,
  input  [7:0] Valor_a_atribuir,
  input  Clock,
  input  in_4,
  input  [1:0] \Endereço ,
  output [7:0] R_XX
);

  wire controlled_buffer_1_out, demultiplexer_1_out0, demultiplexer_1_out1, demultiplexer_1_out2,
       demultiplexer_1_out3;
  wire [7:0] \main_1_saída , \main_2_saída , \main_3_saída , \main_4_saída ;

  Demultiplexer #(.select(2)) demultiplexer_1 (
    .out0(demultiplexer_1_out0), .out1(demultiplexer_1_out1), .out2(demultiplexer_1_out2),
    .out3(demultiplexer_1_out3), .in(controlled_buffer_1_out), .sel(\Endereço ));  // open: en
  assign controlled_buffer_1_out = in_4 ? Clock : 1'bz;  // Controlled_Buffer controlled_buffer_1
  main main_1 (.Clock(demultiplexer_1_out0), .Clear(Clear), .Dado(Valor_a_atribuir), .\Saída (\main_1_saída ));
  main main_2 (.Clock(demultiplexer_1_out1), .Clear(Clear), .Dado(Valor_a_atribuir), .\Saída (\main_2_saída ));
  main main_3 (.Clock(demultiplexer_1_out2), .Clear(Clear), .Dado(Valor_a_atribuir), .\Saída (\main_3_saída ));
  main main_4 (.Clock(demultiplexer_1_out3), .Clear(Clear), .Dado(Valor_a_atribuir), .\Saída (\main_4_saída ));
  Multiplexer #(.select(2), .width(8), .enable("false")) multiplexer_1 (
    .in0(\main_1_saída ), .in1(\main_2_saída ), .in2(\main_3_saída ), .in3(\main_4_saída ), .out(R_XX),
    .sel(\Endereço ));
endmodule

module BD_com_2_Registradores (
  input  Clear,
  input  [7:0] Valor_RA,
  input  [7:0] Valor_RB,
  input  Store_A,
  input  Store_B,
  input  [1:0] \Endereço_RA ,
  input  [1:0] \Endereço_RB ,
  output [7:0] \RA_Endereço ,
  output [7:0] \RB_Endereço 
);

  wire Clock_out;

  Clock Clock (.out(Clock_out));
  BR br_1 (
    .Valor_a_atribuir(Valor_RA), .Clock(Clock_out), .in_4(Store_B), .Clear(Clear),
    .\Endereço (\Endereço_RA ), .R_XX(\RA_Endereço ));
  BR br_2 (
    .Valor_a_atribuir(Valor_RB), .Clock(Clock_out), .in_4(Store_A), .Clear(Clear),
    .\Endereço (\Endereço_RB ), .R_XX(\RB_Endereço ));
endmodule
