// Logisim project D.circ as structural Verilog: 2 circuits, main circuit main
module main (
  input  Entrada,
  input  Preset,
  input  Clear,
  output Saida
);

  wire Pulso_de_Clock_out;

  Clock Pulso_de_Clock (.out(Pulso_de_Clock_out));
  D_Flip_Flop d_ff_1 (
    .clk(Pulso_de_Clock_out), .D(Entrada), .Q(Saida), .preset(Preset), .reset(Clear));  // open: Qn, en
endmodule

module Circuito_D (
  input  nPreset,
  input  D,
  input  nClear,
  output Q,
  output nQ
);

  wire Clock_out, nand_1_out, nand_2_out, nand_3_out, nand_4_out, nand_5_out, nand_6_out, not_1_out,
       not_2_out;

  Clock Clock (.out(Clock_out));
  not not_1 (not_1_out, D);
  nand nand_1 (nand_1_out, D, Clock_out, nQ);
  nand nand_2 (nand_2_out, Q, Clock_out, not_1_out);
  nand nand_3 (nand_3_out, nPreset, nand_1_out, nand_4_out);
  nand nand_4 (nand_4_out, nand_3_out, nand_2_out, nClear);
  not not_2 (not_2_out, Clock_out);
  nand nand_5 (nand_5_out, nClear, nand_3_out, not_2_out);
  nand nand_6 (nand_6_out, not_2_out, nand_4_out, nPreset);
  nand nand_7 (Q, nPreset, nand_5_out, nQ);
  nand nand_8 (nQ, Q, nand_6_out, nClear);
endmodule
