// Logisim project JK.circ as structural Verilog: 2 circuits, main circuit main
module main (
  input  J,
  input  K,
  input  Clear,
  input  Preset,
  output \Saída 
);

  wire Pulso_de_Clock_out;

  Clock Pulso_de_Clock (.out(Pulso_de_Clock_out));
  J_K_Flip_Flop j_k_ff_1 (
    .J(J), .clk(Pulso_de_Clock_out), .K(K), .Q(\Saída ), .preset(Preset), .reset(Clear));  // open: Qn, en
endmodule

module Circuito_JK (
  input  nPreset,
  input  J,
  input  K,
  input  nClear,
  output Q,
  output nQ
);

  wire Clock_out, nand_1_out, nand_2_out, nand_3_out, nand_4_out, nand_5_out, nand_6_out, not_1_out;

  Clock Clock (.out(Clock_out));
  nand nand_1 (nand_1_out, J, Clock_out, nQ);
  nand nand_2 (nand_2_out, Q, Clock_out, K);
  nand nand_3 (nand_3_out, nPreset, nand_1_out, nand_4_out);
  nand nand_4 (nand_4_out, nand_3_out, nand_2_out, nClear);
  not not_1 (not_1_out, Clock_out);
  nand nand_5 (nand_5_out, nClear, nand_3_out, not_1_out);
  nand nand_6 (nand_6_out, not_1_out, nand_4_out, nPreset);
  nand nand_7 (Q, nPreset, nand_5_out, nQ);
  nand nand_8 (nQ, Q, nand_6_out, nClear);
endmodule
