// Logisim project Memoria RAM.circ as structural Verilog: 2 circuits, main circuit main
module main (
  input  in_1,
  input  in_2,
  input  in_3,
  input  in_4,
  input  in_5,
  input  in_6,
  input  in_7,
  input  in_8,
  input  [1:0] in_9,
  input  in_10,
  input  in_11,
  input  in_12,
  output [7:0] out_13
);

  wire clock_1_out, not_1_out;

  Clock clock_1 (.out(clock_1_out));
  RAM #(.addrWidth(2)) ram_1 (.addr(in_9), .data(out_13), .sel(in_10), .clk(clock_1_out), .ld(in_11), .clr(in_12));
  assign out_13 = not_1_out ? {in_1, in_2, in_3, in_4, in_5, in_6, in_7, in_8} : 8'bz;  // Controlled_Buffer controlled_buffer_1
  not not_1 (not_1_out, in_11);
endmodule

module Circuito_RAM (
  input  Clock,
  input  [7:0] Entrada,
  input  [1:0] Endereco,
  input  LW_Read,
  input  Select,
  input  Clear,
  output [7:0] Saida
);

  wire demultiplexer_1_out0, demultiplexer_1_out1, demultiplexer_1_out2, demultiplexer_1_out3, not_1_out;
  wire [1:0] controlled_buffer_1_out;
  wire [7:0] demultiplexer_2_out0, demultiplexer_2_out1, demultiplexer_2_out2, demultiplexer_2_out3,
       register_1_q, register_2_q, register_3_q, register_4_q;

  assign controlled_buffer_1_out = Select ? Endereco : 2'bz;  // Controlled_Buffer controlled_buffer_1
  not not_1 (not_1_out, LW_Read);
  Demultiplexer #(.select(2)) demultiplexer_1 (
    .out0(demultiplexer_1_out0), .out1(demultiplexer_1_out1), .out2(demultiplexer_1_out2),
    .out3(demultiplexer_1_out3), .in(Clock), .sel(controlled_buffer_1_out), .en(not_1_out));
  Demultiplexer #(.select(2), .width(8)) demultiplexer_2 (
    .out0(demultiplexer_2_out0), .out1(demultiplexer_2_out1), .out2(demultiplexer_2_out2),
    .out3(demultiplexer_2_out3), .in(Entrada), .sel(controlled_buffer_1_out), .en(not_1_out));
  Register register_1 (
    .D(demultiplexer_2_out1), .Q(register_1_q), .clk(demultiplexer_1_out1), .clr(Clear));  // open: en
  Register register_2 (
    .D(demultiplexer_2_out0), .Q(register_2_q), .clk(demultiplexer_1_out0), .clr(Clear));  // open: en
  Multiplexer #(.select(2), .width(8)) multiplexer_1 (
    .in0(register_2_q), .in1(register_1_q), .in2(register_3_q), .in3(register_4_q), .out(Saida),
    .sel(controlled_buffer_1_out), .en(LW_Read));
  Register register_3 (
    .D(demultiplexer_2_out2), .Q(register_3_q), .clk(demultiplexer_1_out2), .clr(Clear));  // open: en
  Register register_4 (
    .D(demultiplexer_2_out3), .Q(register_4_q), .clk(demultiplexer_1_out3), .clr(Clear));  // open: en
endmodule
