// Logisim project Multiplexador 4x1.circ as structural Verilog: 1 circuit, main circuit main
module main (
  input  End1,
  input  End2,
  input  A,
  input  B,
  input  C,
  input  D,
  output S
);

  wire and_1_out, and_2_out, and_3_out, and_4_out, not_1_out, not_2_out, not_3_out, not_4_out;

  and and_1 (and_1_out, A, not_1_out, not_2_out);
  not not_1 (not_1_out, End2);
  not not_2 (not_2_out, End1);
  and and_2 (and_2_out, B, End2, not_3_out);
  not not_3 (not_3_out, End1);
  not not_4 (not_4_out, End2);
  and and_3 (and_3_out, C, not_4_out, End1);
  and and_4 (and_4_out, D, End2, End1);
  or or_1 (S, and_1_out, and_2_out, and_3_out, and_4_out);
endmodule
