// Logisim project Máquina de estado.circ as structural Verilog: 1 circuit, main circuit main
module main (
  input  P,
  output R
);

  wire and_1_out, and_2_out, and_3_out, and_4_out, and_5_out, Clock_out, d_ff_1_q, d_ff_2_q, d_ff_3_q,
       not_1_out, xor_1_out, xor_2_out;

  Clock Clock (.out(Clock_out));
  D_Flip_Flop d_ff_1 (.clk(Clock_out), .D(not_1_out), .Q(d_ff_1_q));  // open: Qn, preset, en, reset
  not not_1 (not_1_out, P);
  LED B (.in(and_1_out));
  LED C (.in(and_3_out));
  LED A (.in(d_ff_1_q));
  and and_1 (and_1_out, d_ff_2_q, ~d_ff_3_q, ~R);  // AND_Gate
  D_Flip_Flop d_ff_2 (.clk(Clock_out), .D(P), .Q(d_ff_2_q));  // open: Qn, preset, en, reset
  and and_2 (and_2_out, ~d_ff_1_q, xor_1_out);  // AND_Gate
  LED D (.in(and_5_out));
  D_Flip_Flop d_ff_3 (.clk(Clock_out), .D(and_2_out), .Q(d_ff_3_q));  // open: Qn, preset, en, reset
  xor xor_1 (xor_1_out, d_ff_2_q, R);
  and and_3 (and_3_out, d_ff_3_q, ~d_ff_1_q, ~R);  // AND_Gate
  and and_4 (and_4_out, ~d_ff_1_q, xor_2_out);  // AND_Gate
  xor xor_2 (xor_2_out, R, d_ff_3_q);
  and and_5 (and_5_out, ~d_ff_1_q, R);  // AND_Gate
  D_Flip_Flop d_ff_4 (.clk(Clock_out), .D(and_4_out), .Q(R));  // open: Qn, preset, en, reset
endmodule
