// Logisim project ULA.circ as structural Verilog: 3 circuits, main circuit main
module main (
  input  [7:0] A,
  input  [7:0] B,
  input  [3:0] in_3,
  output [7:0] out_4
);

  wire [7:0] adder_1_out, and_1_out, nand_1_out, nor_1_out, not_1_out, or_1_out, shifter_1_out,
       shifter_2_out, subtractor_1_out, xor_1_out;

  assign and_1_out = A & B;  // AND_Gate and_1, 8 bits wide
  assign or_1_out = A | B;  // OR_Gate or_1, 8 bits wide
  assign not_1_out = ~A;  // NOT_Gate not_1, 8 bits wide
  assign nor_1_out = ~(A | B);  // NOR_Gate nor_1, 8 bits wide
  assign nand_1_out = ~(A & B);  // NAND_Gate nand_1, 8 bits wide
  assign xor_1_out = A ^ B;  // XOR_Gate xor_1, 8 bits wide
  Shifter shifter_1 (.in(A), .\dist (3'b011), .out(shifter_1_out));
  Shifter #(.shift("lr")) shifter_2 (.in(A), .\dist (3'b011), .out(shifter_2_out));
  Adder adder_1 (.a(A), .b(B), .out(adder_1_out));  // open: cin, cout
  Subtractor subtractor_1 (.a(A), .b(B), .out(subtractor_1_out));  // open: bin, bout
  Multiplexer #(.select(4), .width(8), .enable("false")) multiplexer_1 (
    .in0(and_1_out), .in1(or_1_out), .in2(not_1_out), .in3(nor_1_out), .in4(nand_1_out), .in5(xor_1_out),
    .in6(shifter_1_out), .in7(shifter_2_out), .in8(adder_1_out), .in9(subtractor_1_out), .out(out_4),
    .sel(in_3));  // open: in10, in11, in12, in13, in14, in15

  // Notes on the sheet:
  //   0000 - AND
  //   0001 - OR
  //   0010 - NOT
  //   0011 - NOR
  //   0100 - NAND
  //   0101 - XOR
  //   0110 - Shift 3 Bits Esquerda
  //   0111 - Shift 3 Bits Direita
  //   1000 - Soma
  //   1001 - Subtração
endmodule

module Shift_Esquerda (
  input  [7:0] in_1,
  output [7:0] out_2
);


  assign out_2 = {in_1[4:0], 3'b000};
endmodule

module Shift_Direita (
  input  [7:0] in_1,
  output [7:0] out_2
);


  assign out_2 = {3'b000, in_1[7:3]};
endmodule
