// Logisim project Unidade de Controle.circ as structural Verilog: 1 circuit, main circuit main
module main (
  input  [2:0] in_1,
  output REGDEST,
  output ALU_Src,
  output Memto_Reg,
  output Reg_Write,
  output MemRead,
  output MemWrite,
  output Branch,
  output AluOp10,
  output AluOp01,
  output Jump
);

  Multiplexer #(.select(3), .width(10)) multiplexer_1 (
    .in0(10'h240), .in1(10'h1e6), .in2(10'h116), .in3(10'h146), .in4(10'ha), .in5(10'h1), .in6(10'h2c1),
    .in7(10'h144),
    .out({REGDEST, ALU_Src, Memto_Reg, Reg_Write, MemRead, MemWrite, Branch, AluOp10, AluOp01, Jump}),
    .sel(in_1));  // open: en

  // Notes on the sheet:
  //   000 - R-Type
  //   001 - LW
  //   010 - SW
  //   011 - ADDI
  //   100 - BEQ
  //   101 - J
  //   110 - JAL
  //   111 - SLTI
endmodule
